# Fritzing sketch RotationalTrainer (saved by Fritzing 0.9.9b)
breadboards: 2

parts:
  IC1 = 2.8 inch LCD SPI display with touch screen & SD card
  U1 = ESP32S-HiLetgo [part_number=ESP32S-HiLetgo]
  C1 = Ceramic Capacitor [capacitance=2.2mF voltage=6.3V package="0805 [SMD, multilayer]"]
  Part1 = Thumb Joystick
  S3 = Pushbutton [package="[SMD]"]
  S4 = Pushbutton [package="[SMD]"]
  S5 = Pushbutton [package="[SMD]"]
  S6 = Pushbutton [package="[SMD]"]
  R1 = Resistor [tolerance=±5% power=0.25 resistance=1k package=THT]
  R2 = Resistor [tolerance=±5% power=0.25 resistance=1k package=THT]
  R3 = Resistor [tolerance=±5% power=0.25 resistance=1k package=THT]
  R4 = Resistor [tolerance=±5% power=0.25 resistance=1k package=THT]

nets:
  N1: IC1.pin1, IC1.pin8, U1.3.3, Part1.VCC, S3.Pin_3, S3.Pin_4, S4.Pin_3, S4.Pin_4, S5.Pin_3, S5.Pin_4, S6.Pin_3, S6.Pin_4
  GND: IC1.pin2, U1.GND, C1.1, Part1.GND, R1.Pin_1, R2.Pin_1, R3.Pin_1, R4.Pin_0
  N2: IC1.pin3, U1.GPIO15
  N3: IC1.pin4, U1.GPIO4
  N4: IC1.pin5, U1.GPIO2
  N5: IC1.pin6, U1.GPIO23
  N6: IC1.pin7, U1.GPIO18
  N7: U1.EN, C1.0
  N8: U1.GPIO36, Part1.HORZ
  N9: U1.GPIO39, Part1.VERT
  N10: U1.GPIO32, Part1.SEL
  N11: U1.GPIO33, S3.Pin_1, S3.Pin_2, R4.Pin_1
  N12: U1.GPIO25, S4.Pin_1, S4.Pin_2, R2.Pin_0
  N13: U1.GPIO26, S5.Pin_1, S5.Pin_2, R3.Pin_0
  N14: U1.GPIO27, S6.Pin_1, S6.Pin_2, R1.Pin_0

custom parts:
  2.8 inch LCD SPI display with touch screen & SD card: A generic 2.8 inch LCD TFT 320x280 display with touchscreen and SD card slot.
  ESP32S-HiLetgo: HiLetgo ESP-WROOM-32 ESP32 ESP-32S Development Board 2.4GHz Dual-Mode WiFi + Bluetooth Dual Cores Microcontroller The ESP32 integrated with Antenna switches, RF Balun, power amplifiers, low-noise amplifiers, filters, and management modules, and the entire solution occupies the least area of PCB. 2.4 GHz Wi-Fi plus Bluetooth dual-mode chip, with TSMC Ultra-low power consumption 40nm technology,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
